# Fritzing sketch schematic (saved by Fritzing 0.9.6b)
breadboards: 1

parts:
  DHT1 = Humidity and Temperature Sensor DHT11
  M1 = BME280
  A1 = GUVA-S12SD
  WeMos_D1_Mini1 = WeMos D1 Mini

nets (from the breadboard view):
  VCC: DHT1.Vcc, M1.VIN, A1.Pin_3, WeMos_D1_Mini1.3V3
  N1: DHT1.Data-signal, WeMos_D1_Mini1.D1
  N2: DHT1.GND_1, M1.GND, A1.Pin_2, WeMos_D1_Mini1.G
  N3: M1.SCL, WeMos_D1_Mini1.D4
  N4: M1.SDA, WeMos_D1_Mini1.D3
  N5: A1.Pin_1, WeMos_D1_Mini1.A0

custom parts:
  Humidity and Temperature Sensor DHT11: Digital relative humidity & temperature sensor DHT11
  BME280: Temperature Humidity Barometric presure Sensor
  GUVA-S12SD: GUVA-S12SD S12SD UV Detection Light Intensity Sensor Ultraviolet.
